# Fritzing sketch ArduinoStandalone (saved by Fritzing 0.9.3b)
breadboards: 1

parts:
  U2 = ATmega 328P [package=dip]
  Part1 = Arduino Uno (Rev3) - ICSP
  Pullup = Resistor [tolerance=±5% resistance=10k package="2512 [SMD]"]
  C2 = Ceramic Capacitor [capacitance=100pF package="0603 [SMD, multilayer]"]
  L7805_5V_Regulator = Voltage Regulator [package=to-220-alt]
  C3 = Ceramic Capacitor [capacitance=0.33µF package="0603 [SMD, multilayer]"]
  C4 = Ceramic Capacitor [capacitance=0.33µF package="0603 [SMD, multilayer]"]
  XTAL1 = Crystal [frequency="16 Mhz" package=SMD]
  C1 = Ceramic Capacitor [capacitance=100pF package="0603 [SMD, multilayer]"]

nets:
  N1: U2.PC6_(PCINT14/^RESET)_[RESET], Part1.D10_PWM/SS, Pullup.Pin_1
  VCC: U2.VCC, U2.AVCC, Part1.5V, Pullup.Pin_0
  GND: U2.GND, Part1.GND, C2.0, C1.0
  N2: U2.PB6_(PCINT6/XTAL1/TOSC1)_[XTAL1], C2.1, XTAL1.pin_1
  N3: U2.PB7_(PCINT7/XTAL2/TOSC2)_[XTAL2], XTAL1.pin_0, C1.1
  N4: U2.PB3_(MOSI/OC2A/PCINT3)_[D11_PWM], Part1.D11_PWM/MOSI
  N5: U2.PB4_(MISO/PCINT4)_[D12], Part1.D12/MISO
  N6: U2.PB5_(SCK/PCINT5)_[D13], Part1.ICSP_SCK, Part1.D13/SCK
  N7: L7805_5V_Regulator.IN, C3.1
  N8: L7805_5V_Regulator.OUT, C4.1

custom parts:
  ATmega 328P: Atmel ATmega 328P-PU Microcontroller
