# Fritzing sketch espProgrammingInterface (saved by Fritzing 0.9.6b)
perfboards: 1

parts:
  U1 = ESP8266 WiFi Module [part_number=ESP8266]
  Part2 = I2C level shifter bidirectional
  Part3 = FTDI Basic Programmer
  U2 = V_REG_LD1117VXX [package=78xxl]
  5V_Supply = Power Jack [package=power_jack_pth_lock]
  C1 = Ceramic Capacitor [capacitance="100 nF" voltage=35V package="1206 [SMD, multilayer]"]
  Reset_Button = Pushbutton [package="[SMD]"]
  C2 = Ceramic Capacitor [capacitance=10µF voltage=35V package="200 mil [THT, multilayer]"]

nets:
  N1: U1.RXD, Part2.LV2
  N2: U1.VCC, U1.CH_PD, Part2.LV, U2.OUT, C2.1
  GND: U1.GPIO_0, U1.GND, Part2.GND, Part3.GND, U2.GND, 5V_Supply.GND, C1.0, Reset_Button.Pin_1, Reset_Button.Pin_2, C2.0
  N3: U1.RST, Reset_Button.Pin_3, Reset_Button.Pin_4
  N4: U1.TXD, Part2.LV1
  N5: Part2.HV1, Part3.RXI
  N6: Part2.HV2, Part3.TXO
  N7: Part2.HV, U2.IN, 5V_Supply.PWR, C1.1

custom parts:
  ESP8266 WiFi Module: Generic WiFi Module based on the ESP8266 with onboard PCB antenna and UART communications
